// Logisim project test1_solutions.circ as structural Verilog: 5 circuits, main circuit Q1
module Q1 (
  input  A,
  input  B,
  input  C,
  output out
);

  wire and_1_out, not_1_out, not_2_out, not_3_out, not_4_out, or_1_out, or_2_out, or_3_out, or_4_out;

  not not_1 (not_1_out, C);
  not not_2 (not_2_out, A);
  or or_1 (or_1_out, A, not_2_out);
  and and_1 (and_1_out, A, not_1_out);
  or or_2 (or_2_out, not_2_out, B);
  not not_3 (not_3_out, or_1_out);
  not not_4 (not_4_out, and_1_out);
  or or_3 (or_3_out, not_3_out, not_4_out);
  or or_4 (or_4_out, or_3_out, or_2_out);
  not not_5 (out, or_4_out);

  // Notes on the sheet:
  //   ¬((¬A V B) V ¬(A /\ ¬C) V ¬(A V ¬A))
  //   ¬((¬A V B) V ¬(A /\ C))
  //   A /\ ¬B /\ ¬C
endmodule

module Q2 (
  input  A,
  input  B,
  input  C,
  input  D,
  output out
);

  wire and_1_out, and_2_out, not_1_out, not_2_out, not_3_out;

  not not_1 (not_1_out, C);
  not not_2 (not_2_out, B);
  not not_3 (not_3_out, D);
  and and_1 (and_1_out, B, not_1_out);
  and and_2 (and_2_out, not_2_out, not_3_out);
  or or_1 (out, and_1_out, and_2_out);

  // Notes on the sheet:
  //   6 gates: 10 marks, 7 gates: 5 marks, 8 gates: 4 marks, 9 gates: 2 marks, 10+ gates: 1 mark
endmodule

module Q3 (
  input  [15:0] in,
  input  load,
  input  [2:0] address,
  output [15:0] out
);

  wire clock_1_out, demultiplexer_1_out0, demultiplexer_1_out1, demultiplexer_1_out2, demultiplexer_1_out3,
       demultiplexer_1_out4, demultiplexer_1_out5, demultiplexer_1_out6, demultiplexer_1_out7, not_1_out;
  wire [15:0] register_1_q, register_2_q, register_3_q, register_4_q, register_5_q, register_6_q,
       register_7_q, register_8_q;

  Demultiplexer #(.select(3)) demultiplexer_1 (
    .out0(demultiplexer_1_out0), .out1(demultiplexer_1_out1), .out2(demultiplexer_1_out2),
    .out3(demultiplexer_1_out3), .out4(demultiplexer_1_out4), .out5(demultiplexer_1_out5),
    .out6(demultiplexer_1_out6), .out7(demultiplexer_1_out7), .in(load), .sel(address));  // open: en
  Clock clock_1 (.out(clock_1_out));
  not not_1 (not_1_out, clock_1_out);
  Register #(.width(16)) register_1 (
    .D(in), .en(demultiplexer_1_out0), .Q(register_1_q), .clk(not_1_out));  // open: clr
  Register #(.width(16)) register_2 (
    .D(in), .en(demultiplexer_1_out1), .Q(register_2_q), .clk(not_1_out));  // open: clr
  Register #(.width(16)) register_3 (
    .D(in), .en(demultiplexer_1_out2), .Q(register_3_q), .clk(not_1_out));  // open: clr
  Register #(.width(16)) register_4 (
    .D(in), .en(demultiplexer_1_out3), .Q(register_4_q), .clk(not_1_out));  // open: clr
  Register #(.width(16)) register_5 (
    .D(in), .en(demultiplexer_1_out4), .Q(register_5_q), .clk(not_1_out));  // open: clr
  Register #(.width(16)) register_6 (
    .D(in), .en(demultiplexer_1_out5), .Q(register_6_q), .clk(not_1_out));  // open: clr
  Register #(.width(16)) register_7 (
    .D(in), .en(demultiplexer_1_out6), .Q(register_7_q), .clk(not_1_out));  // open: clr
  Register #(.width(16)) register_8 (
    .D(in), .en(demultiplexer_1_out7), .Q(register_8_q), .clk(not_1_out));  // open: clr
  Multiplexer #(.select(3), .width(16)) multiplexer_1 (
    .in0(register_1_q), .in1(register_2_q), .in2(register_3_q), .in3(register_4_q), .in4(register_5_q),
    .in5(register_6_q), .in6(register_7_q), .in7(register_8_q), .out(out), .sel(address));  // open: en
endmodule

module Q4 (
  input  [1:0] in,
  output out
);

  wire and_1_out, clock_1_out, comparator_1_eq, comparator_2_gt, d_ff_1_qn, nand_1_out, not_1_out, or_1_out;
  wire [1:0] counter_1_q, in_old_q;

  Register #(.width(2)) in_old (.D(in), .Q(in_old_q), .clk(clock_1_out));  // open: en, clr
  Comparator #(.width(2), .mode("unsigned")) comparator_1 (.a(in), .b(in_old_q), .eq(comparator_1_eq));  // open: gt, lt
  Counter #(.width(2), .max('h3), .trigger("falling")) counter_1 (
    .count(comparator_2_gt), .Q(counter_1_q), .clk(clock_1_out), .clr(or_1_out));  // open: load, D, carry
  or or_1 (or_1_out, not_1_out, d_ff_1_qn);
  not not_1 (not_1_out, comparator_1_eq);
  Comparator #(.width(2), .mode("unsigned")) comparator_2 (
    .a(in), .b(counter_1_q), .gt(comparator_2_gt));  // open: eq, lt
  Clock clock_1 (.out(clock_1_out));
  and and_1 (and_1_out, comparator_2_gt, nand_1_out);
  nand nand_1 (nand_1_out, not_1_out, out);
  D_Flip_Flop d_ff_1 (.clk(clock_1_out), .D(and_1_out), .Q(out), .Qn(d_ff_1_qn));  // open: preset, en, reset
endmodule

module Q3_common_error (
  input  [15:0] in,
  input  [2:0] address,
  input  load,
  output [15:0] out
);

  wire clock_1_out;
  wire [15:0] demultiplexer_1_out0, demultiplexer_1_out1, demultiplexer_1_out2, demultiplexer_1_out3,
       demultiplexer_1_out4, demultiplexer_1_out5, demultiplexer_1_out6, demultiplexer_1_out7, register_1_q,
       register_2_q, register_3_q, register_4_q, register_5_q, register_6_q, register_7_q, register_8_q;

  Demultiplexer #(.select(3), .width(16)) demultiplexer_1 (
    .out0(demultiplexer_1_out0), .out1(demultiplexer_1_out1), .out2(demultiplexer_1_out2),
    .out3(demultiplexer_1_out3), .out4(demultiplexer_1_out4), .out5(demultiplexer_1_out5),
    .out6(demultiplexer_1_out6), .out7(demultiplexer_1_out7), .in(in), .sel(address));  // open: en
  Clock clock_1 (.out(clock_1_out));
  Register #(.width(16)) register_1 (
    .D(demultiplexer_1_out0), .en(load), .Q(register_1_q), .clk(clock_1_out));  // open: clr
  Register #(.width(16)) register_2 (
    .D(demultiplexer_1_out1), .en(load), .Q(register_2_q), .clk(clock_1_out));  // open: clr
  Register #(.width(16)) register_3 (
    .D(demultiplexer_1_out2), .en(load), .Q(register_3_q), .clk(clock_1_out));  // open: clr
  Register #(.width(16)) register_4 (
    .D(demultiplexer_1_out3), .en(load), .Q(register_4_q), .clk(clock_1_out));  // open: clr
  Register #(.width(16)) register_5 (
    .D(demultiplexer_1_out4), .en(load), .Q(register_5_q), .clk(clock_1_out));  // open: clr
  Register #(.width(16)) register_6 (
    .D(demultiplexer_1_out5), .en(load), .Q(register_6_q), .clk(clock_1_out));  // open: clr
  Register #(.width(16)) register_7 (
    .D(demultiplexer_1_out6), .en(load), .Q(register_7_q), .clk(clock_1_out));  // open: clr
  Register #(.width(16)) register_8 (
    .D(demultiplexer_1_out7), .en(load), .Q(register_8_q), .clk(clock_1_out));  // open: clr
  Multiplexer #(.select(3), .width(16)) multiplexer_1 (
    .in0(register_1_q), .in1(register_2_q), .in2(register_3_q), .in3(register_4_q), .in4(register_5_q),
    .in5(register_6_q), .in6(register_7_q), .in7(register_8_q), .out(out), .sel(address));  // open: en
endmodule
