// Logisim project skeleton.circ as structural Verilog
module Q1 (
  input  A,
  input  B,
  input  C,
  output Out
);
endmodule

module Q2 (
  input  A,
  input  B,
  input  C,
  input  D,
  output Out
);
endmodule

module Q3 (
  input  D,
  input  Clk,
  output Q,
  output Q_prime
);
endmodule

module Q4 (
  output [7:0] out
);

  Button in ();  // open: out
  RAM #(.addrWidth(6), .bus("separate")) ram_1 ();  // open: addr, din, data, str, sel, clk, ld, clr
endmodule
