// Logisim project solutions.circ as structural Verilog
module Q1 (
  input  A,
  input  B,
  input  C,
  input  A_2,
  input  B_2,
  input  C_2,
  output Out,
  output Out_2
);

  wire and_1_out, and_2_out, not_1_out, not_2_out, not_3_out, not_4_out, or_1_out, or_3_out;

  and and_1 (and_1_out, A, B);
  not not_1 (not_1_out, B);
  not not_2 (not_2_out, A_2);
  and and_2 (and_2_out, and_1_out, C);
  or or_1 (or_1_out, not_1_out, C);
  or or_2 (Out_2, not_2_out, B_2);
  not not_3 (not_3_out, or_1_out);
  not not_4 (not_4_out, A);
  or or_3 (or_3_out, and_2_out, not_3_out);
  or or_4 (Out, not_4_out, or_3_out);

  // Notes on the sheet:
  //   Example circuits that would recieve full marks
  //   The above circuit is created directly from the Boolean expression
  //   The below circuit is created by first fully simplifying the Boolean expression
endmodule

module Q2 (
  input  A,
  input  B,
  input  C,
  input  D,
  output Out
);

  wire and_1_out, and_2_out, not_1_out, not_2_out, not_3_out, or_1_out;

  not not_1 (not_1_out, A);
  not not_2 (not_2_out, B);
  not not_3 (not_3_out, D);
  and and_1 (and_1_out, not_2_out, C);
  and and_2 (and_2_out, C, not_3_out);
  or or_1 (or_1_out, not_1_out, and_1_out);
  or or_2 (Out, or_1_out, and_2_out);

  // Notes on the sheet:
  //   Example circuit that would recieve full marks
  //   This is created from the formula ¬A ∨ (¬B ∧ C) ∨ (C ∧ ¬D)
endmodule

module Q3 (
  input  D,
  input  Clk,
  output Q,
  output Q_prime
);

  wire nand_1_out, nand_2_out, nand_3_out, nand_4_out, nand_5_out, nand_6_out, nand_7_out;

  nand nand_1 (nand_1_out, Clk, Clk);
  nand nand_2 (nand_2_out, D, nand_1_out);
  nand nand_3 (nand_3_out, nand_2_out, nand_1_out);
  nand nand_4 (nand_4_out, nand_2_out, nand_5_out);
  nand nand_5 (nand_5_out, nand_4_out, nand_3_out);
  nand nand_6 (nand_6_out, nand_4_out, Clk);
  nand nand_7 (nand_7_out, nand_6_out, Clk);
  nand nand_8 (Q, nand_6_out, Q_prime);
  nand nand_9 (Q_prime, Q, nand_7_out);

  // Notes on the sheet:
  //   Example circuit that would recieve full marks
endmodule

module Q4 (
  output [7:0] out
);

  wire and_1_out, clock_1_out, clock_2_out, d_ff_1_q, in_out, not_1_out;
  wire [5:0] counter_1_q;

  Button in (.out(in_out));
  not not_1 (not_1_out, in_out);
  Counter #(.width(6), .max('h1f)) counter_1 (
    .load(1'b0), .count(1'b1), .Q(counter_1_q), .clk(clock_1_out), .clr(and_1_out));  // open: D, carry
  Clock clock_1 (.out(clock_1_out));
  and and_1 (and_1_out, not_1_out, d_ff_1_q);
  D_Flip_Flop d_ff_1 (.clk(clock_1_out), .D(not_1_out), .Q(d_ff_1_q));  // open: Qn, preset, en, reset
  Clock clock_2 (.out(clock_2_out));
  RAM #(.addrWidth(6), .bus("separate")) ram_1 (
    .addr(counter_1_q), .data(out), .str(1'b0), .clk(clock_2_out), .ld(1'b1));  // open: din, sel, clr
endmodule
