// Logisim project skeleton.circ as structural Verilog: 4 circuits, main circuit Q2
module Q1 (
  input  A,
  input  B,
  input  C,
  output Out
);
endmodule

module Q2 (
  input  A,
  input  B,
  input  C,
  input  D,
  output Out
);
endmodule

module Q3 (
  input  C_in,
  input  [3:0] A,
  input  [3:0] B,
  output [3:0] Sum,
  output C_out
);
endmodule

module Q4 (
  input  [1:0] In,
  output Out,
  output Current_state
);
endmodule
