// Logisim project solutions.circ as structural Verilog
module Q1 (
  input  A,
  input  B,
  input  C,
  input  A_2,
  input  B_2,
  input  C_2,
  output Out,
  output Out_2
);

  wire and_1_out, and_2_out, and_4_out, not_1_out, not_2_out, not_3_out, or_1_out, or_2_out;

  or or_1 (or_1_out, A_2, B_2);
  not not_1 (not_1_out, C_2);
  or or_2 (or_2_out, A, B);
  and and_1 (and_1_out, B, C);
  and and_2 (and_2_out, A, and_1_out);
  and and_3 (Out_2, or_1_out, not_1_out);
  not not_2 (not_2_out, and_2_out);
  not not_3 (not_3_out, C);
  and and_4 (and_4_out, or_2_out, not_2_out);
  and and_5 (Out, and_4_out, not_3_out);
endmodule

module Q2 (
  input  A,
  input  B,
  input  C,
  input  D,
  output Out
);

  wire and_1_out, and_2_out, and_3_out, not_1_out, not_2_out, not_3_out, or_1_out;

  not not_1 (not_1_out, B);
  not not_2 (not_2_out, C);
  not not_3 (not_3_out, D);
  and and_1 (and_1_out, A, C);
  and and_2 (and_2_out, not_1_out, not_3_out);
  and and_3 (and_3_out, not_3_out, not_2_out);
  or or_1 (or_1_out, and_1_out, and_2_out);
  or or_2 (Out, or_1_out, and_3_out);
endmodule

module Q3 (
  input  C_in,
  input  [3:0] A,
  input  [3:0] B,
  output [3:0] Sum,
  output C_out
);

  wire full_adder_1_c_out, full_adder_2_c_out, full_adder_3_c_out;

  Full_adder full_adder_1 (.A(A[0]), .B(B[0]), .C_in(C_in), .C_out(full_adder_1_c_out), .Sum(Sum[0]));
  Full_adder full_adder_2 (.A(A[1]), .B(B[1]), .C_in(full_adder_1_c_out), .C_out(full_adder_2_c_out), .Sum(Sum[1]));
  Full_adder full_adder_3 (.A(A[2]), .B(B[2]), .C_in(full_adder_2_c_out), .C_out(full_adder_3_c_out), .Sum(Sum[2]));
  Full_adder full_adder_4 (.A(A[3]), .B(B[3]), .C_in(full_adder_3_c_out), .C_out(C_out), .Sum(Sum[3]));
endmodule

module Q4 (
  input  [1:0] In,
  output Out,
  output State
);

  wire and_1_out, and_2_out, clock_1_out, not_1_out, not_2_out, not_3_out, or_1_out;

  not not_1 (not_1_out, In[0]);
  not not_2 (not_2_out, State);
  and and_1 (and_1_out, not_1_out, not_2_out);
  and and_2 (and_2_out, In[0], State);
  Clock clock_1 (.out(clock_1_out));
  not not_3 (not_3_out, clock_1_out);
  or or_1 (or_1_out, and_1_out, and_2_out);
  D_Flip_Flop d_ff_1 (.clk(not_3_out), .D(or_1_out), .Q(Out));  // open: Qn, preset, en, reset
  D_Flip_Flop d_ff_2 (.clk(not_3_out), .D(In[1]), .Q(State));  // open: Qn, preset, en, reset
endmodule

module Full_adder (
  input  C_in,
  input  A,
  input  B,
  output Sum,
  output C_out
);

  wire and_1_out, and_2_out, xor_1_out;

  xor xor_1 (xor_1_out, A, B);
  and and_1 (and_1_out, A, B);
  and and_2 (and_2_out, xor_1_out, C_in);
  xor xor_2 (Sum, C_in, xor_1_out);
  or or_1 (C_out, and_2_out, and_1_out);
endmodule
