// Logisim project test-1-solutions.circ as structural Verilog: 8 circuits, main circuit Q7
module Q1 (
  input  A,
  input  B,
  input  C,
  output Out
);

  wire and_1_out, and_2_out, not_1_out, not_2_out;

  not not_1 (not_1_out, B);
  not not_2 (not_2_out, C);
  and and_1 (and_1_out, A, not_1_out);
  and and_2 (and_2_out, B, not_2_out);
  or or_1 (Out, and_1_out, and_2_out);
endmodule

module Q2 (
  input  Sel,
  input  A,
  input  B,
  output Out
);

  wire and_1_out, and_2_out, not_1_out;

  not not_1 (not_1_out, Sel);
  and and_1 (and_1_out, B, Sel);
  and and_2 (and_2_out, A, not_1_out);
  or or_1 (Out, and_1_out, and_2_out);
endmodule

module Q3 (
  input  A,
  input  B,
  input  C,
  input  D,
  output Out
);

  wire and_1_out, and_2_out, and_3_out, and_4_out, not_1_out, not_2_out, not_3_out, or_1_out;

  not not_1 (not_1_out, A);
  not not_2 (not_2_out, C);
  not not_3 (not_3_out, D);
  and and_1 (and_1_out, not_1_out, B);
  and and_2 (and_2_out, not_2_out, D);
  and and_3 (and_3_out, and_1_out, not_3_out);
  and and_4 (and_4_out, C, not_3_out);
  or or_1 (or_1_out, and_3_out, and_4_out);
  or or_2 (Out, or_1_out, and_2_out);
endmodule

module Q4 (
  input  A,
  input  B,
  input  C,
  input  D,
  output Out
);

  wire and_1_out, and_2_out, nor_1_out, not_1_out, or_1_out;

  not not_1 (not_1_out, A);
  and and_1 (and_1_out, not_1_out, B);
  and and_2 (and_2_out, C, D);
  nor nor_1 (nor_1_out, A, C);
  or or_1 (or_1_out, and_1_out, nor_1_out);
  or or_2 (Out, or_1_out, and_2_out);
endmodule

module Q5 (
  input  In,
  output Out
);

  wire and_1_out, clock_1_out, d_ff_1_q, not_1_out;

  not not_1 (not_1_out, d_ff_1_q);
  Clock clock_1 (.out(clock_1_out));
  and and_1 (and_1_out, not_1_out, In);
  D_Flip_Flop #(.trigger("falling")) d_ff_1 (.clk(clock_1_out), .D(In), .Q(d_ff_1_q));  // open: Qn, preset, en, reset
  D_Flip_Flop #(.trigger("falling")) d_ff_2 (.clk(clock_1_out), .D(and_1_out), .Q(Out));  // open: Qn, preset, en, reset
endmodule

module Q6 (
  input  ZX,
  input  NX,
  input  ZY,
  input  NY,
  input  F,
  input  NO,
  input  [3:0] X,
  input  [3:0] Y,
  output [3:0] Out
);

  wire [3:0] adder_1_out, and_1_out, multiplexer_1_out, multiplexer_2_out, multiplexer_3_out,
       multiplexer_4_out, multiplexer_5_out, not_1_out, not_2_out, not_3_out;

  Multiplexer #(.width(4), .enable("false")) multiplexer_1 (.in0(X), .in1(4'b0000), .out(multiplexer_1_out), .sel(ZX));
  assign not_1_out = ~multiplexer_1_out;  // NOT_Gate not_1, 4 bits wide
  Multiplexer #(.width(4), .enable("false")) multiplexer_2 (
    .in0(multiplexer_1_out), .in1(not_1_out), .out(multiplexer_2_out), .sel(NX));
  Multiplexer #(.width(4), .enable("false")) multiplexer_3 (.in0(Y), .in1(4'b0000), .out(multiplexer_3_out), .sel(ZY));
  Multiplexer #(.width(4), .enable("false")) multiplexer_4 (
    .in0(multiplexer_3_out), .in1(not_2_out), .out(multiplexer_4_out), .sel(NY));
  assign not_2_out = ~multiplexer_3_out;  // NOT_Gate not_2, 4 bits wide
  Adder #(.width(4)) adder_1 (
    .a(multiplexer_2_out), .b(multiplexer_4_out), .out(adder_1_out), .cin(1'b0));  // open: cout
  assign and_1_out = multiplexer_2_out & multiplexer_4_out;  // AND_Gate and_1, 4 bits wide
  Multiplexer #(.width(4), .enable("false")) multiplexer_5 (
    .in0(and_1_out), .in1(adder_1_out), .out(multiplexer_5_out), .sel(F));
  assign not_3_out = ~multiplexer_5_out;  // NOT_Gate not_3, 4 bits wide
  Multiplexer #(.width(4), .enable("false")) multiplexer_6 (
    .in0(multiplexer_5_out), .in1(not_3_out), .out(Out), .sel(NO));
endmodule

module Q7 (
  input  Up,
  input  Down,
  input  Left,
  input  Right,
  output [3:0] Pos
);

  wire clock_1_out, or_1_out, or_2_out;
  wire [1:0] y_q;

  or or_1 (or_1_out, Up, Down);
  or or_2 (or_2_out, Left, Right);
  Clock clock_1 (.out(clock_1_out));
  Counter #(.width(1), .max('h1), .ongoal("stay")) y (
    .load(Down), .count(or_1_out), .Q(y_q[0]), .clk(clock_1_out));  // open: D, carry, clr
  Counter #(.width(1), .max('h1), .ongoal("stay")) x (
    .load(Left), .count(or_2_out), .Q(y_q[1]), .clk(clock_1_out));  // open: D, carry, clr
  Multiplexer #(.select(2), .width(4), .enable("false")) multiplexer_1 (
    .in0(4'b0001), .in1(4'b0010), .in2(4'b0100), .in3(4'b1000), .out(Pos), .sel(y_q));
endmodule

module Q8 (
  input  Start_Stop,
  input  [3:0] In,
  input  Reset,
  input  Snooze,
  output [3:0] Out
);

  wire and_1_out, and_2_out, clock_1_out, nor_1_out, not_1_out, not_2_out, or_1_out;
  wire [3:0] multiplexer_1_out;

  not not_1 (not_1_out, Reset);
  and and_1 (and_1_out, Snooze, nor_1_out);
  Multiplexer #(.width(4), .enable("false")) multiplexer_1 (
    .in0(In), .in1(4'b0101), .out(multiplexer_1_out), .sel(and_1_out));
  not not_2 (not_2_out, and_1_out);
  or or_1 (or_1_out, Reset, and_1_out, and_2_out);
  and and_2 (and_2_out, Start_Stop, not_2_out, not_1_out);
  Counter #(.width(4), .max('hf), .ongoal("stay")) counter_1 (
    .load(or_1_out), .D(multiplexer_1_out), .count(and_2_out), .Q(Out), .clk(clock_1_out));  // open: carry, clr
  Clock clock_1 (.out(clock_1_out));
  nor nor_1 (nor_1_out, Out[0], Out[1], Out[2], Out[3]);
  LED Timer (.in(nor_1_out));
endmodule
