// Logisim project test_1_skeleton.circ as structural Verilog: 8 circuits, main circuit Q7
module Q1 (
  input  A,
  input  B,
  input  C,
  output Out
);
endmodule

module Q2 (
  input  Sel,
  input  A,
  input  B,
  output Out
);
endmodule

module Q3 (
  input  A,
  input  B,
  input  C,
  input  D,
  output Out
);
endmodule

module Q4 (
  input  A,
  input  B,
  input  C,
  input  D,
  output Out
);
endmodule

module Q5 (
  input  In,
  output Out
);

  Clock clock_1 ();  // open: out
endmodule

module Q6 (
  input  ZX,
  input  NX,
  input  ZY,
  input  NY,
  input  F,
  input  NO,
  input  [3:0] X,
  input  [3:0] Y,
  output [3:0] Out
);
endmodule

module Q7 (
  input  Up,
  input  Down,
  input  Left,
  input  Right,
  output [3:0] Pos
);

  Clock clock_1 ();  // open: out
endmodule

module Q8 (
  input  Start_Stop,
  input  [3:0] In,
  input  Reset,
  input  Snooze,
  output [3:0] Out
);

  Clock clock_1 ();  // open: out
  LED Timer ();  // open: in
endmodule
