// Logisim project solutions.circ as structural Verilog
module circuit1 (
  input  A,
  input  B,
  input  C,
  input  A_2,
  input  B_2,
  input  C_2,
  output Out,
  output Out_2
);

  wire and_1_out, and_2_out, or_1_out, or_2_out;

  or or_1 (or_1_out, A_2, B_2);
  and and_1 (and_1_out, A, C);
  and and_2 (and_2_out, B, C);
  and and_3 (Out_2, or_1_out, C_2);
  or or_2 (or_2_out, and_1_out, and_2_out);
  and and_4 (Out, or_2_out, C);
endmodule

module circuit2 (
  input  A,
  input  B,
  input  C,
  input  A_2,
  input  B_2,
  input  C_2,
  output Out,
  output Out_2
);

  wire and_1_out, and_2_out, not_1_out, not_2_out, or_1_out;

  and and_1 (and_1_out, B, C);
  not not_1 (not_1_out, A_2);
  and and_2 (and_2_out, B_2, C_2);
  not not_2 (not_2_out, and_1_out);
  and and_3 (Out_2, not_1_out, and_2_out);
  or or_1 (or_1_out, A, not_2_out);
  not not_3 (Out, or_1_out);
endmodule

module circuit3 (
  input  A,
  input  B,
  input  C,
  input  A_2,
  input  B_2,
  input  C_2,
  output Out,
  output Out_2
);

  wire and_1_out, not_1_out, or_1_out, or_2_out;

  not not_1 (not_1_out, B);
  or or_1 (or_1_out, A, B);
  or or_2 (or_2_out, A, not_1_out);
  or or_3 (Out_2, A_2, C_2);
  and and_1 (and_1_out, or_1_out, or_2_out);
  or or_4 (Out, and_1_out, C);
endmodule

module circuit4 (
  input  A,
  input  B,
  input  C,
  input  A_2,
  input  B_2,
  input  C_2,
  output Out,
  output Out_2
);

  wire and_1_out, not_1_out, not_2_out, not_3_out, or_1_out, or_2_out;

  not not_1 (not_1_out, A);
  not not_2 (not_2_out, C_2);
  and and_1 (and_1_out, A, B);
  or or_1 (or_1_out, not_1_out, C);
  or or_2 (or_2_out, B_2, not_2_out);
  or or_3 (Out, and_1_out, not_3_out);
  not not_3 (not_3_out, or_1_out);
  and and_2 (Out_2, A_2, or_2_out);
endmodule

module circuit5 (
  input  A,
  input  B,
  input  C,
  input  A_2,
  input  B_2,
  input  C_2,
  output Out,
  output Out_2
);

  wire and_1_out, and_2_out, or_1_out;

  and and_1 (and_1_out, B_2, C_2);
  or or_1 (or_1_out, A, C);
  or or_2 (Out_2, A_2, and_1_out);
  and and_2 (and_2_out, B, or_1_out);
  or or_3 (Out, A, and_2_out);
endmodule

module circuit6 (
  input  A,
  input  B,
  input  C,
  input  A_2,
  input  B_2,
  input  C_2,
  output Out,
  output Out_2
);

  wire and_1_out, and_2_out, and_3_out, and_4_out, not_1_out, not_2_out;

  and and_1 (and_1_out, A, B);
  and and_2 (and_2_out, A_2, B_2);
  not not_1 (not_1_out, C_2);
  and and_3 (and_3_out, and_1_out, C);
  or or_1 (Out_2, and_2_out, not_1_out);
  not not_2 (not_2_out, and_3_out);
  not not_3 (Out, and_4_out);
  and and_4 (and_4_out, not_2_out, C);
endmodule

module kmap1 (
  input  A,
  input  B,
  input  C,
  output Out
);

  wire not_1_out, not_2_out;

  not not_1 (not_1_out, A);
  not not_2 (not_2_out, C);
  or or_1 (Out, not_1_out, not_2_out);
endmodule

module kmap2 (
  input  A,
  input  B,
  input  C,
  output Out
);

  wire and_1_out, not_1_out, not_2_out;

  not not_1 (not_1_out, B);
  not not_2 (not_2_out, C);
  and and_1 (and_1_out, A, not_2_out);
  or or_1 (Out, not_1_out, and_1_out);
endmodule

module kmap3 (
  input  A,
  input  B,
  input  C,
  output Out
);

  wire and_1_out, and_2_out, not_1_out, not_2_out;

  not not_1 (not_1_out, A);
  not not_2 (not_2_out, C);
  and and_1 (and_1_out, not_1_out, C);
  and and_2 (and_2_out, B, not_2_out);
  or or_1 (Out, and_1_out, and_2_out);
endmodule

module not_nand (
  input  A,
  output Out
);

  nand nand_1 (Out, A, A);
endmodule

module and_nand (
  input  A,
  input  B,
  output Out
);

  wire nand_1_out;

  nand nand_1 (nand_1_out, A, B);
  nand nand_2 (Out, nand_1_out, nand_1_out);
endmodule

module or_nand (
  input  A,
  input  B,
  output Out
);

  wire nand_1_out, nand_2_out;

  nand nand_1 (nand_1_out, A, A);
  nand nand_2 (nand_2_out, B, B);
  nand nand_3 (Out, nand_1_out, nand_2_out);
endmodule

module nor_nand (
  input  A,
  input  B,
  output Out
);

  wire nand_1_out, nand_2_out, nand_3_out;

  nand nand_1 (nand_1_out, A, A);
  nand nand_2 (nand_2_out, B, B);
  nand nand_3 (nand_3_out, nand_1_out, nand_2_out);
  nand nand_4 (Out, nand_3_out, nand_3_out);
endmodule

module xor_nand5 (
  input  A,
  input  B,
  output Out
);

  wire nand_1_out, nand_2_out, nand_3_out, nand_4_out;

  nand nand_1 (nand_1_out, A, A);
  nand nand_2 (nand_2_out, B, B);
  nand nand_3 (nand_3_out, nand_1_out, B);
  nand nand_4 (nand_4_out, A, nand_2_out);
  nand nand_5 (Out, nand_3_out, nand_4_out);
endmodule

module xor_nand4 (
  input  A,
  input  B,
  output Out
);

  wire nand_1_out, nand_2_out, nand_3_out;

  nand nand_1 (nand_1_out, A, B);
  nand nand_2 (nand_2_out, A, nand_1_out);
  nand nand_3 (nand_3_out, nand_1_out, B);
  nand nand_4 (Out, nand_2_out, nand_3_out);
endmodule

module _5vars (
  input  A,
  input  B,
  input  C,
  input  D,
  input  E,
  output Out
);

  wire and_1_out, and_2_out, and_3_out, and_4_out, and_5_out, not_1_out, not_2_out, not_3_out, not_4_out,
       or_1_out;

  not not_1 (not_1_out, A);
  not not_2 (not_2_out, C);
  and and_1 (and_1_out, not_1_out, D);
  not not_3 (not_3_out, D);
  not not_4 (not_4_out, E);
  and and_2 (and_2_out, B, not_2_out);
  and and_3 (and_3_out, not_3_out, not_4_out);
  and and_4 (and_4_out, and_3_out, C);
  and and_5 (and_5_out, and_2_out, D);
  or or_1 (or_1_out, and_1_out, and_4_out);
  or or_2 (Out, or_1_out, and_5_out);
endmodule

module _5vars_nand (
  input  A,
  input  B,
  input  C,
  input  D,
  input  E,
  output Out
);

  wire nand_1_out, nand_2_out, nand_3_out, nand_4_out, nand_5_out, nand_6_out, nand_7_out, nand_8_out,
       nand_9_out, nand_10_out, nand_11_out, nand_12_out, nand_13_out;

  nand nand_1 (nand_1_out, A, A);
  nand nand_2 (nand_2_out, C, C);
  nand nand_3 (nand_3_out, D, D);
  nand nand_4 (nand_4_out, E, E);
  nand nand_5 (nand_5_out, nand_1_out, D);
  nand nand_6 (nand_6_out, C, nand_3_out);
  nand nand_7 (nand_7_out, nand_6_out, nand_6_out);
  nand nand_8 (nand_8_out, nand_2_out, B);
  nand nand_9 (nand_9_out, nand_7_out, nand_4_out);
  nand nand_10 (nand_10_out, nand_8_out, nand_8_out);
  nand nand_11 (nand_11_out, nand_10_out, D);
  nand nand_12 (nand_12_out, nand_5_out, nand_9_out);
  nand nand_13 (nand_13_out, nand_12_out, nand_12_out);
  nand nand_14 (Out, nand_13_out, nand_11_out);
endmodule
