// Logisim project workshop.circ as structural Verilog: 6 circuits, main circuit simplified version
module simplified_version (
  input  N,
  input  E,
  input  S,
  input  W,
  output Out
);

  wire and_1_out, and_2_out, and_3_out, and_4_out, xor_1_out, xor_2_out;

  xor xor_1 (xor_1_out, N, E);
  and and_1 (and_1_out, N, E);
  and and_2 (and_2_out, S, W);
  xor xor_2 (xor_2_out, S, W);
  and and_3 (and_3_out, xor_1_out, and_2_out);
  and and_4 (and_4_out, and_1_out, xor_2_out);
  or or_1 (Out, and_3_out, and_4_out);
endmodule

module kmap_version (
  input  N,
  input  E,
  input  S,
  input  W,
  output Out
);

  wire blue_1_out, green_1_out, or_1_out, or_2_out, red_1_out, yellow_1_out;

  yellow yellow_1 (.N(N), .E(E), .S(S), .W(W), .Out(yellow_1_out));
  red red_1 (.N(N), .E(E), .S(S), .W(W), .Out(red_1_out));
  green green_1 (.N(N), .E(E), .S(S), .W(W), .Out(green_1_out));
  blue blue_1 (.N(N), .E(E), .S(S), .W(W), .Out(blue_1_out));
  or or_1 (or_1_out, green_1_out, blue_1_out);
  or or_2 (or_2_out, red_1_out, or_1_out);
  or or_3 (Out, or_2_out, yellow_1_out);
endmodule

module red (
  input  N,
  input  E,
  input  S,
  input  W,
  output Out
);

  wire and_1_out, and_2_out, not_1_out;

  not not_1 (not_1_out, N);
  and and_1 (and_1_out, not_1_out, E);
  and and_2 (and_2_out, S, W);
  and and_3 (Out, and_1_out, and_2_out);
endmodule

module yellow (
  input  N,
  input  E,
  input  S,
  input  W,
  output Out
);

  wire and_1_out, and_2_out, not_1_out;

  not not_1 (not_1_out, E);
  and and_1 (and_1_out, N, not_1_out);
  and and_2 (and_2_out, S, W);
  and and_3 (Out, and_1_out, and_2_out);
endmodule

module green (
  input  N,
  input  E,
  input  S,
  input  W,
  output Out
);

  wire and_1_out, and_2_out, not_1_out;

  not not_1 (not_1_out, S);
  and and_1 (and_1_out, N, E);
  and and_2 (and_2_out, not_1_out, W);
  and and_3 (Out, and_1_out, and_2_out);
endmodule

module blue (
  input  N,
  input  E,
  input  S,
  input  W,
  output Out
);

  wire and_1_out, and_2_out, not_1_out;

  not not_1 (not_1_out, W);
  and and_1 (and_1_out, N, E);
  and and_2 (and_2_out, and_1_out, S);
  and and_3 (Out, and_2_out, not_1_out);
endmodule
