// Logisim project labsheet_answers.circ as structural Verilog: 10 circuits, main circuit half_adder
module half_adder (
  input  A,
  input  B,
  output S,
  output C_out
);

  xor xor_1 (S, A, B);
  and and_1 (C_out, A, B);
endmodule

module _4bit_incrementer (
  input  [3:0] A,
  output C_out,
  output [3:0] S
);

  wire half_adder_2_c_out, half_adder_3_c_out, half_adder_4_c_out;

  half_adder half_adder_1 (.A(A[3]), .B(half_adder_2_c_out), .C_out(C_out), .S(S[3]));
  half_adder half_adder_2 (.A(A[2]), .B(half_adder_3_c_out), .C_out(half_adder_2_c_out), .S(S[2]));
  half_adder half_adder_3 (.A(A[1]), .B(half_adder_4_c_out), .C_out(half_adder_3_c_out), .S(S[1]));
  half_adder half_adder_4 (.A(A[0]), .B(1'b1), .C_out(half_adder_4_c_out), .S(S[0]));
endmodule

module full_adder (
  input  A,
  input  B,
  input  C_in,
  output S,
  output C_out
);

  wire and_1_out, and_2_out, xor_1_out;

  xor xor_1 (xor_1_out, A, B);
  and and_1 (and_1_out, A, B);
  xor xor_2 (S, xor_1_out, C_in);
  and and_2 (and_2_out, C_in, xor_1_out);
  or or_1 (C_out, and_2_out, and_1_out);
endmodule

module _4bit_adder (
  input  [3:0] A,
  input  [3:0] B,
  input  C_in,
  output C_out,
  output [3:0] S
);

  wire full_adder_2_c_out, full_adder_3_c_out, full_adder_4_c_out;

  full_adder full_adder_1 (.A(A[3]), .B(B[3]), .C_in(full_adder_2_c_out), .C_out(C_out), .S(S[3]));
  full_adder full_adder_2 (.A(A[2]), .B(B[2]), .C_in(full_adder_3_c_out), .C_out(full_adder_2_c_out), .S(S[2]));
  full_adder full_adder_3 (.A(A[1]), .B(B[1]), .C_in(full_adder_4_c_out), .C_out(full_adder_3_c_out), .S(S[1]));
  full_adder full_adder_4 (.A(A[0]), .B(B[0]), .C_in(C_in), .C_out(full_adder_4_c_out), .S(S[0]));
endmodule

module _4bit_adder_subtractor (
  input  _0___Adder__1___Subtractor,
  input  [3:0] A,
  input  [3:0] B,
  output [3:0] S,
  output C_out
);

  wire [3:0] multiplexer_1_out, not_1_out;

  assign not_1_out = ~B;  // NOT_Gate not_1, 4 bits wide
  Multiplexer #(.width(4), .enable("false")) multiplexer_1 (
    .in0(B), .in1(not_1_out), .out(multiplexer_1_out), .sel(_0___Adder__1___Subtractor));
  _4bit_adder u_4bit_adder_1 (.A(multiplexer_1_out), .B(A), .C_out(C_out), .C_in(_0___Adder__1___Subtractor), .S(S));
endmodule

module nand_half_adder (
  input  A,
  input  B,
  output S,
  output C_out
);

  wire nand_1_out, nand_2_out, nand_3_out;

  nand nand_1 (nand_1_out, A, B);
  nand nand_2 (nand_2_out, A, nand_1_out);
  nand nand_3 (nand_3_out, nand_1_out, B);
  nand nand_4 (C_out, nand_1_out, nand_1_out);
  nand nand_5 (S, nand_2_out, nand_3_out);
endmodule

module nand_full_adder (
  input  A,
  input  B,
  input  C_in,
  output S,
  output C_out
);

  wire nand_1_out, nand_2_out, nand_3_out, nand_4_out, nand_5_out, nand_6_out, nand_7_out;

  nand nand_1 (nand_1_out, A, B);
  nand nand_2 (nand_2_out, A, nand_1_out);
  nand nand_3 (nand_3_out, nand_1_out, B);
  nand nand_4 (nand_4_out, nand_2_out, nand_3_out);
  nand nand_5 (nand_5_out, nand_4_out, C_in);
  nand nand_6 (nand_6_out, nand_4_out, nand_5_out);
  nand nand_7 (nand_7_out, nand_5_out, C_in);
  nand nand_8 (C_out, nand_5_out, nand_1_out);
  nand nand_9 (S, nand_6_out, nand_7_out);
endmodule

module nand_3bit_bitwise_incrementer (
  input  A,
  input  A_2,
  input  A_3,
  output S,
  output S_2,
  output S_3,
  output C_out
);

  wire nand_1_out, nand_2_out, nand_3_out, nand_4_out, nand_5_out, nand_6_out, nand_7_out, nand_8_out,
       nand_9_out, nand_10_out, nand_11_out;

  nand nand_1 (nand_1_out, A, 1'b1);
  nand nand_2 (nand_2_out, A_2, nand_6_out);
  nand nand_3 (nand_3_out, A_3, nand_9_out);
  nand nand_4 (nand_4_out, A, nand_1_out);
  nand nand_5 (nand_5_out, nand_1_out, 1'b1);
  nand nand_6 (nand_6_out, nand_1_out, nand_1_out);
  nand nand_7 (nand_7_out, A_2, nand_2_out);
  nand nand_8 (nand_8_out, nand_2_out, nand_6_out);
  nand nand_9 (nand_9_out, nand_2_out, nand_2_out);
  nand nand_10 (nand_10_out, A_3, nand_3_out);
  nand nand_11 (nand_11_out, nand_3_out, nand_9_out);
  nand nand_12 (C_out, nand_3_out, nand_3_out);
  nand nand_13 (S, nand_4_out, nand_5_out);
  nand nand_14 (S_2, nand_7_out, nand_8_out);
  nand nand_15 (S_3, nand_10_out, nand_11_out);
endmodule

module plexers (
  input  [3:0] A,
  input  [3:0] B,
  input  E,
  input  [1:0] C,
  input  D,
  output [3:0] Output
);

  wire demultiplexer_1_out0;
  wire [3:0] and_1_out, nor_1_out, or_1_out, xor_1_out;

  assign and_1_out = A & B;  // AND_Gate and_1, 4 bits wide
  assign or_1_out = A | B;  // OR_Gate or_1, 4 bits wide
  assign xor_1_out = A ^ B;  // XOR_Gate xor_1, 4 bits wide
  assign nor_1_out = ~(A | B);  // NOR_Gate nor_1, 4 bits wide
  Multiplexer #(.select(2), .width(4)) multiplexer_1 (
    .in0(and_1_out), .in1(or_1_out), .in2(xor_1_out), .in3(nor_1_out), .out(Output), .sel(C),
    .en(demultiplexer_1_out0));
  Demultiplexer #(.enable("false")) demultiplexer_1 (.out0(demultiplexer_1_out0), .in(E), .sel(D));  // open: out1
endmodule

module alu (
  input  zx,
  input  nx,
  input  zy,
  input  ny,
  input  f,
  input  no,
  input  [3:0] x,
  input  [3:0] y,
  output [3:0] out_9,
  output ng,
  output zr
);

  wire [3:0] and_1_out, multiplexer_1_out, multiplexer_2_out, multiplexer_3_out, multiplexer_4_out,
       multiplexer_5_out, n4bit_adder_1_s, not_1_out, not_2_out, not_3_out;

  Multiplexer #(.width(4), .enable("false")) multiplexer_1 (.in0(x), .in1(4'b0000), .out(multiplexer_1_out), .sel(zx));
  assign not_1_out = ~multiplexer_1_out;  // NOT_Gate not_1, 4 bits wide
  Multiplexer #(.width(4), .enable("false")) multiplexer_2 (
    .in0(multiplexer_1_out), .in1(not_1_out), .out(multiplexer_2_out), .sel(nx));
  Multiplexer #(.width(4), .enable("false")) multiplexer_3 (.in0(y), .in1(4'b0000), .out(multiplexer_3_out), .sel(zy));
  Multiplexer #(.width(4), .enable("false")) multiplexer_4 (
    .in0(multiplexer_3_out), .in1(not_2_out), .out(multiplexer_4_out), .sel(ny));
  assign not_2_out = ~multiplexer_3_out;  // NOT_Gate not_2, 4 bits wide
  _4bit_adder u_4bit_adder_1 (
    .A(multiplexer_4_out), .B(multiplexer_2_out), .C_in(1'b0), .S(n4bit_adder_1_s));  // open: C_out
  assign and_1_out = multiplexer_2_out & multiplexer_4_out;  // AND_Gate and_1, 4 bits wide
  Multiplexer #(.width(4), .enable("false")) multiplexer_5 (
    .in0(and_1_out), .in1(n4bit_adder_1_s), .out(multiplexer_5_out), .sel(f));
  assign not_3_out = ~multiplexer_5_out;  // NOT_Gate not_3, 4 bits wide
  Multiplexer #(.width(4), .enable("false")) multiplexer_6 (
    .in0(multiplexer_5_out), .in1(not_3_out), .out({ng, out_9[2:0]}), .sel(no));
  nor nor_1 (zr, out_9[0], out_9[1], out_9[2], ng);

  assign out_9[3] = ng;
endmodule
