// Logisim project solutions.circ as structural Verilog: 12 circuits, main circuit half adder
module half_adder (
  input  A,
  input  B,
  output S,
  output C_out
);

  xor xor_1 (S, A, B);
  and and_1 (C_out, A, B);
endmodule

module _4_bit_incrementer (
  input  [3:0] A,
  output C_out,
  output [3:0] S
);

  wire half_adder_2_c_out, half_adder_3_c_out, half_adder_4_c_out;

  half_adder half_adder_1 (.A(A[3]), .B(half_adder_2_c_out), .C_out(C_out), .S(S[3]));
  half_adder half_adder_2 (.A(A[2]), .B(half_adder_3_c_out), .C_out(half_adder_2_c_out), .S(S[2]));
  half_adder half_adder_3 (.A(A[1]), .B(half_adder_4_c_out), .C_out(half_adder_3_c_out), .S(S[1]));
  half_adder half_adder_4 (.A(A[0]), .B(1'b1), .C_out(half_adder_4_c_out), .S(S[0]));
endmodule

module full_adder (
  input  A,
  input  B,
  input  C_in,
  output S,
  output C_out
);

  wire and_1_out, and_2_out, xor_1_out;

  xor xor_1 (xor_1_out, A, B);
  and and_1 (and_1_out, A, B);
  xor xor_2 (S, xor_1_out, C_in);
  and and_2 (and_2_out, C_in, xor_1_out);
  or or_1 (C_out, and_2_out, and_1_out);
endmodule

module _4_bit_adder (
  input  [3:0] A,
  input  [3:0] B,
  input  C_in,
  output C_out,
  output [3:0] S
);

  wire full_adder_2_c_out, full_adder_3_c_out, full_adder_4_c_out;

  full_adder full_adder_1 (.A(A[3]), .B(B[3]), .C_in(full_adder_2_c_out), .C_out(C_out), .S(S[3]));
  full_adder full_adder_2 (.A(A[2]), .B(B[2]), .C_in(full_adder_3_c_out), .C_out(full_adder_2_c_out), .S(S[2]));
  full_adder full_adder_3 (.A(A[1]), .B(B[1]), .C_in(full_adder_4_c_out), .C_out(full_adder_3_c_out), .S(S[1]));
  full_adder full_adder_4 (.A(A[0]), .B(B[0]), .C_in(C_in), .C_out(full_adder_4_c_out), .S(S[0]));
endmodule

module _4_bit_adder_subtractor (
  input  _0___Adder__1___Subtractor,
  input  [3:0] A,
  input  [3:0] B,
  output [3:0] S,
  output C_out
);

  wire [3:0] multiplexer_1_out, not_1_out;

  assign not_1_out = ~B;  // NOT_Gate not_1, 4 bits wide
  Multiplexer #(.width(4), .enable("false")) multiplexer_1 (
    .in0(B), .in1(not_1_out), .out(multiplexer_1_out), .sel(_0___Adder__1___Subtractor));
  _4_bit_adder u_4_bit_adder_1 (.A(multiplexer_1_out), .B(A), .C_out(C_out), .C_in(_0___Adder__1___Subtractor), .S(S));
endmodule

module nand_half_adder (
  input  A,
  input  B,
  output S,
  output C_out
);

  wire nand_1_out, nand_2_out, nand_3_out;

  nand nand_1 (nand_1_out, A, B);
  nand nand_2 (nand_2_out, A, nand_1_out);
  nand nand_3 (nand_3_out, nand_1_out, B);
  nand nand_4 (C_out, nand_1_out, nand_1_out);
  nand nand_5 (S, nand_2_out, nand_3_out);
endmodule

module nand_full_adder (
  input  A,
  input  B,
  input  C_in,
  output S,
  output C_out
);

  wire nand_1_out, nand_2_out, nand_3_out, nand_4_out, nand_5_out, nand_6_out, nand_7_out;

  nand nand_1 (nand_1_out, A, B);
  nand nand_2 (nand_2_out, A, nand_1_out);
  nand nand_3 (nand_3_out, nand_1_out, B);
  nand nand_4 (nand_4_out, nand_2_out, nand_3_out);
  nand nand_5 (nand_5_out, nand_4_out, C_in);
  nand nand_6 (nand_6_out, nand_4_out, nand_5_out);
  nand nand_7 (nand_7_out, nand_5_out, C_in);
  nand nand_8 (C_out, nand_5_out, nand_1_out);
  nand nand_9 (S, nand_6_out, nand_7_out);
endmodule

module _2_1_mux (
  input  In0,
  input  In1,
  input  Sel,
  output Out
);

  wire and_1_out, and_2_out, not_1_out;

  not not_1 (not_1_out, Sel);
  and and_1 (and_1_out, In0, not_1_out);
  and and_2 (and_2_out, In1, Sel);
  or or_1 (Out, and_1_out, and_2_out);
endmodule

module _1_2_demux (
  input  In,
  input  Sel,
  output Out0,
  output Out1
);

  wire not_1_out;

  not not_1 (not_1_out, Sel);
  and and_1 (Out0, In, not_1_out);
  and and_2 (Out1, In, Sel);
endmodule

module _4_1_mux (
  input  In0,
  input  In1,
  input  In2,
  input  In3,
  input  [1:0] Sel,
  output Out
);

  wire n2_1_mux_1_out, n2_1_mux_2_out;

  _2_1_mux u_2_1_mux_1 (.In0(In0), .In1(In1), .Sel(Sel[0]), .Out(n2_1_mux_1_out));
  _2_1_mux u_2_1_mux_2 (.In0(In2), .In1(In3), .Sel(Sel[0]), .Out(n2_1_mux_2_out));
  _2_1_mux u_2_1_mux_3 (.In0(n2_1_mux_1_out), .In1(n2_1_mux_2_out), .Sel(Sel[1]), .Out(Out));
endmodule

module _1_4_demux (
  input  In,
  input  [1:0] Sel,
  output Out0,
  output Out1,
  output Out2,
  output Out3
);

  wire n1_2_demux_1_out0, n1_2_demux_1_out1;

  _1_2_demux u_1_2_demux_1 (.In(In), .Sel(Sel[1]), .Out0(n1_2_demux_1_out0), .Out1(n1_2_demux_1_out1));
  _1_2_demux u_1_2_demux_2 (.In(n1_2_demux_1_out0), .Sel(Sel[0]), .Out0(Out0), .Out1(Out1));
  _1_2_demux u_1_2_demux_3 (.In(n1_2_demux_1_out1), .Sel(Sel[0]), .Out0(Out2), .Out1(Out3));
endmodule

module alu (
  input  zx,
  input  nx,
  input  zy,
  input  ny,
  input  f,
  input  no,
  input  [3:0] x,
  input  [3:0] y,
  output [3:0] out,
  output ng,
  output zr
);

  wire [3:0] and_1_out, multiplexer_1_out, multiplexer_2_out, multiplexer_3_out, multiplexer_4_out,
       multiplexer_5_out, n4_bit_adder_1_s, not_1_out, not_2_out, not_3_out;

  Multiplexer #(.width(4), .enable("false")) multiplexer_1 (.in0(x), .in1(4'b0000), .out(multiplexer_1_out), .sel(zx));
  assign not_1_out = ~multiplexer_1_out;  // NOT_Gate not_1, 4 bits wide
  Multiplexer #(.width(4), .enable("false")) multiplexer_2 (
    .in0(multiplexer_1_out), .in1(not_1_out), .out(multiplexer_2_out), .sel(nx));
  Multiplexer #(.width(4), .enable("false")) multiplexer_3 (.in0(y), .in1(4'b0000), .out(multiplexer_3_out), .sel(zy));
  Multiplexer #(.width(4), .enable("false")) multiplexer_4 (
    .in0(multiplexer_3_out), .in1(not_2_out), .out(multiplexer_4_out), .sel(ny));
  assign not_2_out = ~multiplexer_3_out;  // NOT_Gate not_2, 4 bits wide
  _4_bit_adder u_4_bit_adder_1 (
    .A(multiplexer_4_out), .B(multiplexer_2_out), .C_in(1'b0), .S(n4_bit_adder_1_s));  // open: C_out
  assign and_1_out = multiplexer_2_out & multiplexer_4_out;  // AND_Gate and_1, 4 bits wide
  Multiplexer #(.width(4), .enable("false")) multiplexer_5 (
    .in0(and_1_out), .in1(n4_bit_adder_1_s), .out(multiplexer_5_out), .sel(f));
  assign not_3_out = ~multiplexer_5_out;  // NOT_Gate not_3, 4 bits wide
  Multiplexer #(.width(4), .enable("false")) multiplexer_6 (
    .in0(multiplexer_5_out), .in1(not_3_out), .out({ng, out[2:0]}), .sel(no));
  nor nor_1 (zr, out[0], out[1], out[2], ng);

  assign out[3] = ng;
endmodule
