// Logisim project solutions.circ as structural Verilog
module R_S_latch__active_low (
  input  S_prime,
  input  R_prime,
  output Q,
  output Q_prime
);

  nand nand_1 (Q, S_prime, Q_prime);
  nand nand_2 (Q_prime, Q, R_prime);
endmodule

module R_S_latch__active_high (
  input  S,
  input  R,
  output Q,
  output Q_prime
);

  wire nand_1_out, nand_2_out;

  nand nand_1 (nand_1_out, S, S);
  nand nand_2 (nand_2_out, R, R);
  nand nand_3 (Q, nand_1_out, Q_prime);
  nand nand_4 (Q_prime, Q, nand_2_out);
endmodule

module D_latch__active_high (
  input  D,
  input  en,
  output Q,
  output Q_prime
);

  wire nand_1_out, nand_2_out;

  nand nand_1 (nand_1_out, D, en);
  nand nand_2 (nand_2_out, nand_1_out, en);
  nand nand_3 (Q, nand_1_out, Q_prime);
  nand nand_4 (Q_prime, Q, nand_2_out);

  // Notes on the sheet:
  //   This is different from the D latch seen in lectures - either is valid!
endmodule

module D_latch__active_low (
  input  D,
  input  en,
  output Q,
  output Q_prime
);

  wire nand_1_out, nand_2_out, nand_3_out;

  nand nand_1 (nand_1_out, en, en);
  nand nand_2 (nand_2_out, D, nand_1_out);
  nand nand_3 (nand_3_out, nand_2_out, nand_1_out);
  nand nand_4 (Q, nand_2_out, Q_prime);
  nand nand_5 (Q_prime, Q, nand_3_out);
endmodule

module D_flip_flop__negative_edge (
  input  D,
  input  en,
  output Q,
  output Q_prime
);

  wire d_latch_active_high_1_q, d_latch_active_high_1_q_prime, nand_1_out;

  D_latch__active_high d_latch_active_high_1 (
    .D(D), .en(en), .Q(d_latch_active_high_1_q), .Q_prime(d_latch_active_high_1_q_prime));
  nand nand_1 (nand_1_out, en, en);
  D_latch__active_high d_latch_active_high_2 (.D(d_latch_active_high_1_q), .en(nand_1_out), .Q(Q), .Q_prime(Q_prime));
endmodule

module D_flip_flop__positive_edge (
  input  D,
  input  en,
  output Q,
  output Q_prime
);

  wire d_latch_active_high_1_q, d_latch_active_high_1_q_prime, nand_1_out;

  D_latch__active_high d_latch_active_high_1 (
    .D(D), .en(nand_1_out), .Q(d_latch_active_high_1_q), .Q_prime(d_latch_active_high_1_q_prime));
  nand nand_1 (nand_1_out, en, en);
  D_latch__active_high d_latch_active_high_2 (.D(d_latch_active_high_1_q), .en(en), .Q(Q), .Q_prime(Q_prime));
endmodule

module T_flip_flop (
  output Q,
  output Q_prime
);

  wire clock_1_out;

  Clock clock_1 (.out(clock_1_out));
  D_Flip_Flop d_ff_1 (.clk(clock_1_out), .D(Q_prime), .Q(Q), .Qn(Q_prime));  // open: preset, en, reset
endmodule

module JK_flip_flop (
  input  J,
  input  K,
  input  Clock,
  output Q,
  output Q_prime
);

  wire and_1_out, and_2_out, not_1_out, or_1_out;

  not not_1 (not_1_out, K);
  and and_1 (and_1_out, Q_prime, J);
  and and_2 (and_2_out, not_1_out, Q);
  or or_1 (or_1_out, and_1_out, and_2_out);
  D_Flip_Flop d_ff_1 (.clk(Clock), .D(or_1_out), .Q(Q), .Qn(Q_prime));  // open: preset, en, reset
endmodule

module RAM8 (
  input  clock,
  input  [15:0] in,
  input  load,
  input  [2:0] address,
  output [15:0] out_5
);

  wire demultiplexer_1_out0, demultiplexer_1_out1, demultiplexer_1_out2, demultiplexer_1_out3,
       demultiplexer_1_out4, demultiplexer_1_out5, demultiplexer_1_out6, demultiplexer_1_out7;
  wire [15:0] register_1_q, register_2_q, register_3_q, register_4_q, register_5_q, register_6_q,
       register_7_q, register_8_q;

  Demultiplexer #(.select(3), .enable("false")) demultiplexer_1 (
    .out0(demultiplexer_1_out0), .out1(demultiplexer_1_out1), .out2(demultiplexer_1_out2),
    .out3(demultiplexer_1_out3), .out4(demultiplexer_1_out4), .out5(demultiplexer_1_out5),
    .out6(demultiplexer_1_out6), .out7(demultiplexer_1_out7), .in(load), .sel(address));
  Register #(.width(16)) register_1 (.D(in), .en(demultiplexer_1_out0), .Q(register_1_q), .clk(clock));  // open: clr
  Register #(.width(16)) register_2 (.D(in), .en(demultiplexer_1_out1), .Q(register_2_q), .clk(clock));  // open: clr
  Register #(.width(16)) register_3 (.D(in), .en(demultiplexer_1_out2), .Q(register_3_q), .clk(clock));  // open: clr
  Register #(.width(16)) register_4 (.D(in), .en(demultiplexer_1_out3), .Q(register_4_q), .clk(clock));  // open: clr
  Register #(.width(16)) register_5 (.D(in), .en(demultiplexer_1_out4), .Q(register_5_q), .clk(clock));  // open: clr
  Register #(.width(16)) register_6 (.D(in), .en(demultiplexer_1_out5), .Q(register_6_q), .clk(clock));  // open: clr
  Register #(.width(16)) register_7 (.D(in), .en(demultiplexer_1_out6), .Q(register_7_q), .clk(clock));  // open: clr
  Register #(.width(16)) register_8 (.D(in), .en(demultiplexer_1_out7), .Q(register_8_q), .clk(clock));  // open: clr
  Multiplexer #(.select(3), .width(16), .enable("false")) multiplexer_1 (
    .in0(register_1_q), .in1(register_2_q), .in2(register_3_q), .in3(register_4_q), .in4(register_5_q),
    .in5(register_6_q), .in6(register_7_q), .in7(register_8_q), .out(out_5), .sel(address));
endmodule

module RAM64 (
  input  clock,
  input  [15:0] in,
  input  load,
  input  [5:0] address,
  output [15:0] out_5
);

  wire demultiplexer_1_out0, demultiplexer_1_out1, demultiplexer_1_out2, demultiplexer_1_out3,
       demultiplexer_1_out4, demultiplexer_1_out5, demultiplexer_1_out6, demultiplexer_1_out7;
  wire [15:0] ram8_1_out_5, ram8_2_out_5, ram8_3_out_5, ram8_4_out_5, ram8_5_out_5, ram8_6_out_5,
       ram8_7_out_5, ram8_8_out_5;

  Demultiplexer #(.select(3), .enable("false")) demultiplexer_1 (
    .out0(demultiplexer_1_out0), .out1(demultiplexer_1_out1), .out2(demultiplexer_1_out2),
    .out3(demultiplexer_1_out3), .out4(demultiplexer_1_out4), .out5(demultiplexer_1_out5),
    .out6(demultiplexer_1_out6), .out7(demultiplexer_1_out7), .in(load), .sel(address[2:0]));
  RAM8 ram8_1 (.clock(clock), .in(in), .load(demultiplexer_1_out0), .address(address[5:3]), .out_5(ram8_1_out_5));
  RAM8 ram8_2 (.clock(clock), .in(in), .load(demultiplexer_1_out1), .address(address[5:3]), .out_5(ram8_2_out_5));
  RAM8 ram8_3 (.clock(clock), .in(in), .load(demultiplexer_1_out2), .address(address[5:3]), .out_5(ram8_3_out_5));
  RAM8 ram8_4 (.clock(clock), .in(in), .load(demultiplexer_1_out3), .address(address[5:3]), .out_5(ram8_4_out_5));
  RAM8 ram8_5 (.clock(clock), .in(in), .load(demultiplexer_1_out4), .address(address[5:3]), .out_5(ram8_5_out_5));
  RAM8 ram8_6 (.clock(clock), .in(in), .load(demultiplexer_1_out5), .address(address[5:3]), .out_5(ram8_6_out_5));
  RAM8 ram8_7 (.clock(clock), .in(in), .load(demultiplexer_1_out6), .address(address[5:3]), .out_5(ram8_7_out_5));
  RAM8 ram8_8 (.clock(clock), .in(in), .load(demultiplexer_1_out7), .address(address[5:3]), .out_5(ram8_8_out_5));
  Multiplexer #(.select(3), .width(16), .enable("false")) multiplexer_1 (
    .in0(ram8_1_out_5), .in1(ram8_2_out_5), .in2(ram8_3_out_5), .in3(ram8_4_out_5), .in4(ram8_5_out_5),
    .in5(ram8_6_out_5), .in6(ram8_7_out_5), .in7(ram8_8_out_5), .out(out_5), .sel(address[2:0]));
endmodule

module RAM512 (
  input  clock,
  input  [15:0] in,
  input  load,
  input  [8:0] address,
  output [15:0] out_5
);

  wire demultiplexer_1_out0, demultiplexer_1_out1, demultiplexer_1_out2, demultiplexer_1_out3,
       demultiplexer_1_out4, demultiplexer_1_out5, demultiplexer_1_out6, demultiplexer_1_out7;
  wire [15:0] ram64_1_out_5, ram64_2_out_5, ram64_3_out_5, ram64_4_out_5, ram64_5_out_5, ram64_6_out_5,
       ram64_7_out_5, ram64_8_out_5;

  Demultiplexer #(.select(3), .enable("false")) demultiplexer_1 (
    .out0(demultiplexer_1_out0), .out1(demultiplexer_1_out1), .out2(demultiplexer_1_out2),
    .out3(demultiplexer_1_out3), .out4(demultiplexer_1_out4), .out5(demultiplexer_1_out5),
    .out6(demultiplexer_1_out6), .out7(demultiplexer_1_out7), .in(load), .sel(address[2:0]));
  RAM64 ram64_1 (.clock(clock), .in(in), .load(demultiplexer_1_out0), .address(address[8:3]), .out_5(ram64_1_out_5));
  RAM64 ram64_2 (.clock(clock), .in(in), .load(demultiplexer_1_out1), .address(address[8:3]), .out_5(ram64_2_out_5));
  RAM64 ram64_3 (.clock(clock), .in(in), .load(demultiplexer_1_out2), .address(address[8:3]), .out_5(ram64_3_out_5));
  RAM64 ram64_4 (.clock(clock), .in(in), .load(demultiplexer_1_out3), .address(address[8:3]), .out_5(ram64_4_out_5));
  RAM64 ram64_5 (.clock(clock), .in(in), .load(demultiplexer_1_out4), .address(address[8:3]), .out_5(ram64_5_out_5));
  RAM64 ram64_6 (.clock(clock), .in(in), .load(demultiplexer_1_out5), .address(address[8:3]), .out_5(ram64_6_out_5));
  RAM64 ram64_7 (.clock(clock), .in(in), .load(demultiplexer_1_out6), .address(address[8:3]), .out_5(ram64_7_out_5));
  RAM64 ram64_8 (.clock(clock), .in(in), .load(demultiplexer_1_out7), .address(address[8:3]), .out_5(ram64_8_out_5));
  Multiplexer #(.select(3), .width(16), .enable("false")) multiplexer_1 (
    .in0(ram64_1_out_5), .in1(ram64_2_out_5), .in2(ram64_3_out_5), .in3(ram64_4_out_5), .in4(ram64_5_out_5),
    .in5(ram64_6_out_5), .in6(ram64_7_out_5), .in7(ram64_8_out_5), .out(out_5), .sel(address[2:0]));
endmodule

module RAM4K (
  input  clock,
  input  [15:0] in,
  input  load,
  input  [11:0] address,
  output [15:0] out_5
);

  wire demultiplexer_1_out0, demultiplexer_1_out1, demultiplexer_1_out2, demultiplexer_1_out3,
       demultiplexer_1_out4, demultiplexer_1_out5, demultiplexer_1_out6, demultiplexer_1_out7;
  wire [15:0] ram512_1_out_5, ram512_2_out_5, ram512_3_out_5, ram512_4_out_5, ram512_5_out_5, ram512_6_out_5,
       ram512_7_out_5, ram512_8_out_5;

  Demultiplexer #(.select(3), .enable("false")) demultiplexer_1 (
    .out0(demultiplexer_1_out0), .out1(demultiplexer_1_out1), .out2(demultiplexer_1_out2),
    .out3(demultiplexer_1_out3), .out4(demultiplexer_1_out4), .out5(demultiplexer_1_out5),
    .out6(demultiplexer_1_out6), .out7(demultiplexer_1_out7), .in(load), .sel(address[2:0]));
  RAM512 ram512_1 (
    .clock(clock), .in(in), .load(demultiplexer_1_out0), .address(address[11:3]), .out_5(ram512_1_out_5));
  RAM512 ram512_2 (
    .clock(clock), .in(in), .load(demultiplexer_1_out1), .address(address[11:3]), .out_5(ram512_2_out_5));
  RAM512 ram512_3 (
    .clock(clock), .in(in), .load(demultiplexer_1_out2), .address(address[11:3]), .out_5(ram512_3_out_5));
  RAM512 ram512_4 (
    .clock(clock), .in(in), .load(demultiplexer_1_out3), .address(address[11:3]), .out_5(ram512_4_out_5));
  RAM512 ram512_5 (
    .clock(clock), .in(in), .load(demultiplexer_1_out4), .address(address[11:3]), .out_5(ram512_5_out_5));
  RAM512 ram512_6 (
    .clock(clock), .in(in), .load(demultiplexer_1_out5), .address(address[11:3]), .out_5(ram512_6_out_5));
  RAM512 ram512_7 (
    .clock(clock), .in(in), .load(demultiplexer_1_out6), .address(address[11:3]), .out_5(ram512_7_out_5));
  RAM512 ram512_8 (
    .clock(clock), .in(in), .load(demultiplexer_1_out7), .address(address[11:3]), .out_5(ram512_8_out_5));
  Multiplexer #(.select(3), .width(16), .enable("false")) multiplexer_1 (
    .in0(ram512_1_out_5), .in1(ram512_2_out_5), .in2(ram512_3_out_5), .in3(ram512_4_out_5),
    .in4(ram512_5_out_5), .in5(ram512_6_out_5), .in6(ram512_7_out_5), .in7(ram512_8_out_5), .out(out_5),
    .sel(address[2:0]));
endmodule

module RAM16K (
  input  clock,
  input  [15:0] in,
  input  load,
  input  [13:0] address,
  output [15:0] out_5
);

  wire demultiplexer_1_out0, demultiplexer_1_out1, demultiplexer_1_out2, demultiplexer_1_out3;
  wire [15:0] ram4k_1_out_5, ram4k_2_out_5, ram4k_3_out_5, ram4k_4_out_5;

  Demultiplexer #(.select(2), .enable("false")) demultiplexer_1 (
    .out0(demultiplexer_1_out0), .out1(demultiplexer_1_out1), .out2(demultiplexer_1_out2),
    .out3(demultiplexer_1_out3), .in(load), .sel(address[1:0]));
  RAM4K ram4k_1 (.clock(clock), .in(in), .load(demultiplexer_1_out0), .address(address[13:2]), .out_5(ram4k_1_out_5));
  RAM4K ram4k_2 (.clock(clock), .in(in), .load(demultiplexer_1_out1), .address(address[13:2]), .out_5(ram4k_2_out_5));
  RAM4K ram4k_3 (.clock(clock), .in(in), .load(demultiplexer_1_out2), .address(address[13:2]), .out_5(ram4k_3_out_5));
  RAM4K ram4k_4 (.clock(clock), .in(in), .load(demultiplexer_1_out3), .address(address[13:2]), .out_5(ram4k_4_out_5));
  Multiplexer #(.select(2), .width(16), .enable("false")) multiplexer_1 (
    .in0(ram4k_1_out_5), .in1(ram4k_2_out_5), .in2(ram4k_3_out_5), .in3(ram4k_4_out_5), .out(out_5),
    .sel(address[1:0]));
endmodule
