// Logisim project workshop.circ as structural Verilog: 1 circuit, main circuit shift register
module shift_register (
  input  left_right,
  input  shift,
  input  wrap_around,
  input  [15:0] in,
  input  load,
  output [15:0] out
);

  wire clock_1_out;
  wire [0:0] multiplexer_5_out;
  wire [15:0] multiplexer_1_out, multiplexer_2_out, multiplexer_3_out;
  wire [15:15] multiplexer_4_out;

  Multiplexer #(.width(16), .enable("false")) multiplexer_1 (
    .in0(out), .in1(multiplexer_3_out), .out(multiplexer_1_out), .sel(shift));
  Multiplexer #(.width(16), .enable("false")) multiplexer_2 (
    .in0(multiplexer_1_out), .in1(in), .out(multiplexer_2_out), .sel(load));
  Multiplexer #(.width(16), .enable("false")) multiplexer_3 (
    .in0({multiplexer_4_out[15], out[15:1]}), .in1({out[14:0], multiplexer_5_out[0]}),
    .out(multiplexer_3_out), .sel(left_right));
  Multiplexer #(.enable("false")) multiplexer_4 (
    .in0(1'b0), .in1(out[0]), .out(multiplexer_4_out[15]), .sel(wrap_around));
  Multiplexer #(.enable("false")) multiplexer_5 (
    .in0(1'b0), .in1(out[15]), .out(multiplexer_5_out[0]), .sel(wrap_around));
  Register #(.width(16), .trigger("falling")) register_1 (
    .D(multiplexer_2_out), .Q(out), .clk(clock_1_out));  // open: en, clr
  Clock clock_1 (.out(clock_1_out));
endmodule
