// Logisim project counter.circ as structural Verilog: 1 circuit, main circuit main
module main (
  input  reset,
  output [15:0] out
);

  wire clock_1_out;
  wire [15:0] adder_1_out, multiplexer_1_out;

  Multiplexer #(.width(16)) multiplexer_1 (
    .in0(adder_1_out), .in1({16{1'b0}}), .out(multiplexer_1_out), .sel(reset));  // open: en
  Register #(.width(16)) register_1 (.D(multiplexer_1_out), .en(1'b1), .Q(out), .clk(clock_1_out));  // open: clr
  Clock clock_1 (.out(clock_1_out));
  Adder #(.width(16)) adder_1 (.a(out), .b(16'h1), .out(adder_1_out), .cin(1'b0));  // open: cout
endmodule
