// Logisim project one-shot_v1.circ as structural Verilog: 1 circuit, main circuit main
module main (
  input  in,
  output out
);

  wire and_1_out, and_2_out, clock_1_out, d_ff_1_q, d_ff_1_qn, d_ff_2_qn, or_1_out;

  Clock clock_1 (.out(clock_1_out));
  and and_1 (and_1_out, or_1_out, in);
  and and_2 (and_2_out, in, d_ff_1_qn, d_ff_2_qn);
  or or_1 (or_1_out, out, d_ff_1_q);
  D_Flip_Flop d_ff_1 (.clk(clock_1_out), .D(and_1_out), .Q(d_ff_1_q), .Qn(d_ff_1_qn));  // open: preset, en, reset
  D_Flip_Flop d_ff_2 (.clk(clock_1_out), .D(and_2_out), .Q(out), .Qn(d_ff_2_qn));  // open: preset, en, reset

  // Notes on the sheet:
  //   X
  //   Y
endmodule
