// Logisim project one-shot_v2.circ as structural Verilog: 1 circuit, main circuit main
module main (
  input  in,
  output out
);

  wire and_1_out, clock_1_out, d_ff_1_q, not_1_out;

  not not_1 (not_1_out, d_ff_1_q);
  and and_1 (and_1_out, not_1_out, in);
  Clock clock_1 (.out(clock_1_out));
  D_Flip_Flop d_ff_1 (.clk(clock_1_out), .D(in), .Q(d_ff_1_q));  // open: Qn, preset, en, reset
  D_Flip_Flop d_ff_2 (.clk(clock_1_out), .D(and_1_out), .Q(out));  // open: Qn, preset, en, reset

  // Notes on the sheet:
  //   Logic
  //   Storage
  //   State
  //   Output
endmodule
