// Logisim project solutions.circ as structural Verilog: 15 circuits, main circuit Rise/fall detector 1
module NOT (
  input  A,
  output Q
);

  Transistor transistor_1 (.in(1'b1), .out(Q), .gate(A));
  Transistor #(.\type ("n")) transistor_2 (.in(1'b0), .out(Q), .gate(A));
endmodule

module NOR (
  input  A,
  input  B,
  output Q
);

  wire transistor_1_out;

  Transistor transistor_1 (.in(1'b1), .out(transistor_1_out), .gate(A));
  Transistor transistor_2 (.in(transistor_1_out), .out(Q), .gate(B));
  Transistor #(.\type ("n")) transistor_3 (.in(1'b0), .out(Q), .gate(A));
  Transistor #(.\type ("n")) transistor_4 (.in(1'b0), .out(Q), .gate(B));
endmodule

module NAND (
  input  A,
  input  B,
  output Q
);

  wire transistor_3_out;

  Transistor transistor_1 (.in(1'b1), .out(Q), .gate(A));
  Transistor #(.\type ("n")) transistor_2 (.in(transistor_3_out), .out(Q), .gate(A));
  Transistor #(.\type ("n")) transistor_3 (.in(1'b0), .out(transistor_3_out), .gate(B));
  Transistor transistor_4 (.in(1'b1), .out(Q), .gate(B));
endmodule

module OR (
  input  A,
  input  B,
  output Q
);

  wire transistor_1_out, transistor_2_out;

  Transistor transistor_1 (.in(1'b1), .out(transistor_1_out), .gate(A));
  Transistor transistor_2 (.in(transistor_1_out), .out(transistor_2_out), .gate(B));
  Transistor #(.\type ("n")) transistor_3 (.in(1'b0), .out(transistor_2_out), .gate(A));
  Transistor #(.\type ("n")) transistor_4 (.in(1'b0), .out(transistor_2_out), .gate(B));
  Transistor transistor_5 (.in(1'b1), .out(Q), .gate(transistor_2_out));
  Transistor #(.\type ("n")) transistor_6 (.in(1'b0), .out(Q), .gate(transistor_2_out));
endmodule

module AND (
  input  A,
  input  B,
  output Q
);

  wire transistor_1_out, transistor_3_out;

  Transistor transistor_1 (.in(1'b1), .out(transistor_1_out), .gate(A));
  Transistor #(.\type ("n")) transistor_2 (.in(transistor_3_out), .out(transistor_1_out), .gate(A));
  Transistor #(.\type ("n")) transistor_3 (.in(1'b0), .out(transistor_3_out), .gate(B));
  Transistor transistor_4 (.in(1'b1), .out(transistor_1_out), .gate(B));
  Transistor transistor_5 (.in(1'b1), .out(Q), .gate(transistor_1_out));
  Transistor #(.\type ("n")) transistor_6 (.in(1'b0), .out(Q), .gate(transistor_1_out));
endmodule

module One_shot (
  input  in,
  output out
);

  wire and_1_out, clock_1_out, not_1_out, state_q;

  not not_1 (not_1_out, state_q);
  and and_1 (and_1_out, not_1_out, in);
  Clock clock_1 (.out(clock_1_out));
  D_Flip_Flop state (.clk(clock_1_out), .D(in), .Q(state_q));  // open: Qn, preset, en, reset
  D_Flip_Flop u_out (.clk(clock_1_out), .D(and_1_out), .Q(out));  // open: Qn, preset, en, reset
endmodule

module Rise_fall_detector_1 (
  input  in,
  output rise,
  output fall
);

  wire not_1_out;

  not not_1 (not_1_out, in);
  One_shot one_shot_1 (.in(in), .out(rise));
  One_shot one_shot_2 (.in(not_1_out), .out(fall));
endmodule

module Rise_fall_detector_2 (
  input  in,
  output rise,
  output fall
);

  wire and_1_out, and_2_out, clock_1_out, not_1_out, state_q, state_qn;

  not not_1 (not_1_out, in);
  Clock clock_1 (.out(clock_1_out));
  and and_1 (and_1_out, state_qn, in);
  and and_2 (and_2_out, state_q, not_1_out);
  D_Flip_Flop state (.clk(clock_1_out), .D(in), .Q(state_q), .Qn(state_qn));  // open: preset, en, reset
  D_Flip_Flop u_rise (.clk(clock_1_out), .D(and_1_out), .Q(rise));  // open: Qn, preset, en, reset
  D_Flip_Flop u_fall (.clk(clock_1_out), .D(and_2_out), .Q(fall));  // open: Qn, preset, en, reset
endmodule

module Program_counter (
  input  [15:0] in,
  input  reset,
  input  inc,
  input  load,
  output [15:0] out
);

  wire clock_1_out, or_1_out;
  wire [15:0] adder_1_out, multiplexer_1_out, multiplexer_2_out;

  Multiplexer #(.width(16), .enable("false")) multiplexer_1 (
    .in0({16{1'b0}}), .in1(adder_1_out), .out(multiplexer_1_out), .sel(inc));
  Multiplexer #(.width(16), .enable("false")) multiplexer_2 (
    .in0(multiplexer_1_out), .in1(in), .out(multiplexer_2_out), .sel(load));
  or or_1 (or_1_out, reset, inc, load);
  Register #(.width(16)) register_1 (.D(multiplexer_2_out), .en(or_1_out), .Q(out), .clk(clock_1_out));  // open: clr
  Clock clock_1 (.out(clock_1_out));
  Adder #(.width(16)) adder_1 (.a(16'h1), .b(out), .out(adder_1_out));  // open: cin, cout
endmodule

module State_transitions (
  input  change,
  output green,
  output amber,
  output red,
  output flash_amber
);

  wire clock_1_out, multiplexer_1_out, multiplexer_2_out, multiplexer_3_out, multiplexer_4_out,
       one_shot_1_out, or_1_out;

  One_shot one_shot_1 (.in(1'b1), .out(one_shot_1_out));
  or or_1 (or_1_out, green, one_shot_1_out);
  Multiplexer #(.enable("false")) multiplexer_1 (
    .in0(or_1_out), .in1(flash_amber), .out(multiplexer_1_out), .sel(change));
  Multiplexer #(.enable("false")) multiplexer_2 (.in0(amber), .in1(green), .out(multiplexer_2_out), .sel(change));
  Multiplexer #(.enable("false")) multiplexer_3 (.in0(red), .in1(amber), .out(multiplexer_3_out), .sel(change));
  Multiplexer #(.enable("false")) multiplexer_4 (.in0(flash_amber), .in1(red), .out(multiplexer_4_out), .sel(change));
  D_Flip_Flop d_ff_1 (.clk(clock_1_out), .D(multiplexer_1_out), .Q(green));  // open: Qn, preset, en, reset
  D_Flip_Flop d_ff_2 (.clk(clock_1_out), .D(multiplexer_2_out), .Q(amber));  // open: Qn, preset, en, reset
  D_Flip_Flop d_ff_3 (.clk(clock_1_out), .D(multiplexer_3_out), .Q(red));  // open: Qn, preset, en, reset
  D_Flip_Flop d_ff_4 (.clk(clock_1_out), .D(multiplexer_4_out), .Q(flash_amber));  // open: Qn, preset, en, reset
  Clock clock_1 (.out(clock_1_out));
endmodule

module Equal (
  input  [15:0] x,
  input  [15:0] y,
  output out
);

  wire [15:0] xnor_1_out;

  assign xnor_1_out = ~(x ^ y);  // XNOR_Gate xnor_1, 16 bits wide
  and and_1 (out, xnor_1_out[0], xnor_1_out[1], xnor_1_out[2], xnor_1_out[3], xnor_1_out[4], xnor_1_out[5], xnor_1_out[6], xnor_1_out[7], xnor_1_out[9], xnor_1_out[10], xnor_1_out[11], xnor_1_out[12], xnor_1_out[13], xnor_1_out[14], xnor_1_out[15], xnor_1_out[8]);
endmodule

module Timer (
  input  [15:0] \time ,
  input  start,
  output done
);

  wire and_1_out, and_2_out, clock_1_out, d_ff_1_q, not_1_out, not_2_out;
  wire [15:0] counter_1_q;

  D_Flip_Flop d_ff_1 (.clk(clock_1_out), .D(start), .Q(d_ff_1_q));  // open: Qn, preset, en, reset
  not not_1 (not_1_out, start);
  not not_2 (not_2_out, done);
  and and_1 (and_1_out, d_ff_1_q, not_1_out);
  and and_2 (and_2_out, start, not_2_out);
  Counter #(.width(16), .max('hffff)) counter_1 (
    .count(and_2_out), .Q(counter_1_q), .clk(clock_1_out), .clr(and_1_out));  // open: load, D, carry
  Clock clock_1 (.out(clock_1_out));
  Equal equal_1 (.x(\time ), .y(counter_1_q), .out(done));
endmodule

module Timed_state_transitions (
  input  change,
  output green,
  output amber,
  output red,
  output flash_amber
);

  wire and_1_out, or_1_out, timer_1_done, timer_2_done, timer_3_done;

  and and_1 (and_1_out, green, change);
  or or_1 (or_1_out, and_1_out, timer_1_done, timer_2_done, timer_3_done);
  State_transitions state_transitions_1 (
    .change(or_1_out), .green(green), .amber(amber), .red(red), .flash_amber(flash_amber));
  Timer timer_1 (.\time (16'h400), .start(amber), .done(timer_1_done));
  Timer timer_2 (.\time (16'h1e00), .start(red), .done(timer_2_done));
  Timer timer_3 (.\time (16'ha00), .start(flash_amber), .done(timer_3_done));
endmodule

module Flash_generator (
  input  flash,
  output out
);

  wire and_1_out, and_3_out, d_ff_1_q, d_ff_1_qn, not_1_out, or_1_out, timer_1_done, timer_2_done;

  and and_1 (and_1_out, flash, d_ff_1_qn);
  Timer timer_1 (.\time (16'h199), .start(and_1_out), .done(timer_1_done));
  or or_1 (or_1_out, timer_1_done, timer_2_done);
  D_Flip_Flop d_ff_1 (
    .clk(or_1_out), .D(d_ff_1_qn), .Q(d_ff_1_q), .Qn(d_ff_1_qn), .reset(not_1_out));  // open: preset, en
  not not_1 (not_1_out, flash);
  and and_2 (out, flash, d_ff_1_qn);
  Timer timer_2 (.\time (16'h199), .start(and_3_out), .done(timer_2_done));
  and and_3 (and_3_out, flash, d_ff_1_q);
endmodule

module Traffic_Light (
);

  wire button_1_out, flash_generator_1_out, or_1_out, timed_state_transitions_1_amber,
       timed_state_transitions_1_flash_amber, timed_state_transitions_1_green, timed_state_transitions_1_red;

  Button button_1 (.out(button_1_out));
  Timed_state_transitions timed_state_transitions_1 (
    .change(button_1_out), .green(timed_state_transitions_1_green), .amber(timed_state_transitions_1_amber),
    .red(timed_state_transitions_1_red), .flash_amber(timed_state_transitions_1_flash_amber));
  Flash_generator flash_generator_1 (.flash(timed_state_transitions_1_flash_amber), .out(flash_generator_1_out));
  LED led_1 (.in(timed_state_transitions_1_red));
  LED led_2 (.in(or_1_out));
  or or_1 (or_1_out, timed_state_transitions_1_amber, flash_generator_1_out);
  LED led_3 (.in(timed_state_transitions_1_green));
endmodule
