// Logisim project workshop.circ as structural Verilog: 1 circuit, main circuit main
module main (
  input  In,
  output [1:0] State,
  output Out
);

  wire and_1_out, and_2_out, and_3_out, and_4_out, and_5_out, and_6_out, clock_1_out, nor_1_out, not_1_out,
       not_2_out, not_3_out, or_1_out;

  not not_1 (not_1_out, State[1]);
  and and_1 (and_1_out, not_1_out, State[0]);
  not not_2 (not_2_out, State[0]);
  and and_2 (and_2_out, State[0], State[1]);
  and and_3 (and_3_out, and_1_out, In);
  and and_4 (and_4_out, State[1], not_2_out);
  not not_3 (not_3_out, In);
  nor nor_1 (nor_1_out, State[0], In);
  and and_5 (and_5_out, and_2_out, In);
  or or_1 (or_1_out, and_3_out, and_6_out);
  and and_6 (and_6_out, and_4_out, not_3_out);
  Clock clock_1 (.out(clock_1_out));
  D_Flip_Flop Sa (.clk(clock_1_out), .D(or_1_out), .Q(State[1]));  // open: Qn, preset, en, reset
  D_Flip_Flop Sb (.clk(clock_1_out), .D(nor_1_out), .Q(State[0]));  // open: Qn, preset, en, reset
  D_Flip_Flop u_Out (.clk(clock_1_out), .D(and_5_out), .Q(Out));  // open: Qn, preset, en, reset
endmodule
