// Logisim project skeleton.circ as structural Verilog: 4 circuits, main circuit ALU
module Hack (
  input  reset
);

  ROM #(.addrWidth(15), .dataWidth(16)) rom_1 ();  // open: addr, data, sel
  CPU cpu_1 ();  // open: inM, instruction, reset, writeM, outM, addressM, pc
  RAM #(.addrWidth(15), .dataWidth(16), .bus("separate")) ram_1 ();  // open: addr, din, data, str, sel, clk, ld, clr

  // Notes on the sheet:
  //   contents of rom_1 (hex, n*v repeats v):
  //   0 fc10 20 e308 ec10 10 e308 10 fc20 fc90 77 e302 e7d0 1 e010 1e e302 10 fc20 fc10 f090 f090 e7d0 10
  //   fde0 e308 10 fdc8 7 ea87 10 fc20 fc10 0 e308 1 efc8 1 fc10 11 e308 f ec10 1 f008 e7d0 f4c8 0 fc10 2
  //   e308 1 fc10 51 e302 4000 ec10 e090 2 f010 42 e305 12 ea88 44 ea87 12 efc8 2 fc30 e0b0 2 e308 1 fc88
  //   12 fc10 2 f088 33 ea87 11 fc10 10 e4d0 6c e303 11 e3c8 13 efc8 11 fc10 66 e302 13 fc10 f088 11 fc88
  //   5b ea87 13 fc90 2 f008 6e ea87 2 ea88 2 fc10 10 fde0 e308 10 fdc8 7 ea87 77 ea87
endmodule

module ALU (
  input  zx,
  input  nx,
  input  zy,
  input  ny,
  input  f,
  input  no,
  input  [15:0] x,
  input  [15:0] y,
  output [15:0] out_9
);

  wire [15:0] adder_1_out, and_1_out, multiplexer_1_out, multiplexer_2_out, multiplexer_3_out,
       multiplexer_4_out, multiplexer_5_out, not_1_out, not_2_out, not_3_out;

  Multiplexer #(.width(16), .enable("false")) multiplexer_1 (
    .in0(x), .in1({16{1'b0}}), .out(multiplexer_1_out), .sel(zx));
  assign not_1_out = ~multiplexer_1_out;  // NOT_Gate not_1, 16 bits wide
  Multiplexer #(.width(16), .enable("false")) multiplexer_2 (
    .in0(multiplexer_1_out), .in1(not_1_out), .out(multiplexer_2_out), .sel(nx));
  Multiplexer #(.width(16), .enable("false")) multiplexer_3 (
    .in0(y), .in1({16{1'b0}}), .out(multiplexer_3_out), .sel(zy));
  Multiplexer #(.width(16), .enable("false")) multiplexer_4 (
    .in0(multiplexer_3_out), .in1(not_2_out), .out(multiplexer_4_out), .sel(ny));
  assign not_2_out = ~multiplexer_3_out;  // NOT_Gate not_2, 16 bits wide
  Adder #(.width(16)) adder_1 (
    .a(multiplexer_2_out), .b(multiplexer_4_out), .out(adder_1_out), .cin(1'b0));  // open: cout
  assign and_1_out = multiplexer_2_out & multiplexer_4_out;  // AND_Gate and_1, 16 bits wide
  Multiplexer #(.width(16), .enable("false")) multiplexer_5 (
    .in0(and_1_out), .in1(adder_1_out), .out(multiplexer_5_out), .sel(f));
  assign not_3_out = ~multiplexer_5_out;  // NOT_Gate not_3, 16 bits wide
  Multiplexer #(.width(16), .enable("false")) multiplexer_6 (
    .in0(multiplexer_5_out), .in1(not_3_out), .out(out_9), .sel(no));
endmodule

module Program_counter (
  input  [15:0] in,
  input  reset,
  input  inc,
  input  load,
  output [15:0] out
);

  wire clock_1_out, or_1_out;
  wire [15:0] adder_1_out, multiplexer_1_out, multiplexer_2_out;

  Multiplexer #(.width(16), .enable("false")) multiplexer_1 (
    .in0({16{1'b0}}), .in1(adder_1_out), .out(multiplexer_1_out), .sel(inc));
  Multiplexer #(.width(16), .enable("false")) multiplexer_2 (
    .in0(multiplexer_1_out), .in1(in), .out(multiplexer_2_out), .sel(load));
  or or_1 (or_1_out, reset, inc, load);
  Register #(.width(16)) register_1 (.D(multiplexer_2_out), .en(or_1_out), .Q(out), .clk(clock_1_out));  // open: clr
  Clock clock_1 (.out(clock_1_out));
  Adder #(.width(16)) adder_1 (.a(16'h1), .b(out), .out(adder_1_out), .cin(1'b0));  // open: cout
endmodule

module CPU (
  input  [15:0] inM,
  input  [15:0] instruction,
  input  reset,
  output writeM,
  output [15:0] outM,
  output [14:0] addressM,
  output [14:0] pc
);
endmodule
